// Logisim project 3-bit identity comparator.circ as structural Verilog: 1 circuit, main circuit id_cmp
module id_cmp (
  input  a0,
  input  a1,
  input  a2,
  input  b0,
  input  b1,
  input  b2,
  output q
);

  wire nand_1_out, nand_2_out, nand_3_out, not_1_out, not_2_out, not_3_out, not_4_out, not_5_out, xor_1_out,
       xor_2_out, xor_3_out;

  not not_1 (not_1_out, xor_1_out);
  xor xor_1 (xor_1_out, a0, b0);
  xor xor_2 (xor_2_out, a1, b1);
  not not_2 (not_2_out, xor_2_out);
  xor xor_3 (xor_3_out, a2, b2);
  not not_3 (not_3_out, xor_3_out);
  nand nand_1 (nand_1_out, not_1_out, 1'b1);
  not not_4 (not_4_out, nand_1_out);
  nand nand_2 (nand_2_out, not_2_out, not_3_out);
  not not_5 (not_5_out, nand_2_out);
  nand nand_3 (nand_3_out, not_4_out, not_5_out);
  not not_6 (q, nand_3_out);

  // Notes on the sheet:
  //   3-bit identity comparator
  //   3/4 XOR
  //   3/6 NOT
  //   2/4 NAND
  //   5/6 NOT
  //   3/4 NAND
  //   6/6 NOT
endmodule
