// Logisim project 74f374.circ as structural Verilog: 1 circuit, main circuit 74F374
module _74F374 (
  input  D0,
  input  D1,
  input  D2,
  input  D3,
  input  D4,
  input  D5,
  input  D6,
  input  D7,
  input  nCP,
  input  nOE,
  output Q0,
  output Q1,
  output Q2,
  output Q3,
  output Q4,
  output Q5,
  output Q6,
  output Q7
);

  wire D_0_qn, D_1_qn, D_2_qn, D_3_qn, D_4_qn, D_5_qn, D_6_qn, D_7_qn, not_1_out, not_2_out;

  not not_1 (not_1_out, nCP);
  not not_2 (not_2_out, nOE);
  D_Flip_Flop #(.trigger("falling")) D_0 (
    .clk(not_1_out), .D(D0), .Qn(D_0_qn), .preset(1'b0), .en(1'b1), .reset(1'b0));  // open: Q
  assign Q0 = not_2_out ? ~D_0_qn : 1'bz;  // Controlled_Inverter controlled_inverter_1
  D_Flip_Flop #(.trigger("falling")) D_1 (
    .clk(not_1_out), .D(D1), .Qn(D_1_qn), .preset(1'b0), .en(1'b1), .reset(1'b0));  // open: Q
  assign Q1 = not_2_out ? ~D_1_qn : 1'bz;  // Controlled_Inverter controlled_inverter_2
  D_Flip_Flop #(.trigger("falling")) D_2 (
    .clk(not_1_out), .D(D2), .Qn(D_2_qn), .preset(1'b0), .en(1'b1), .reset(1'b0));  // open: Q
  assign Q2 = not_2_out ? ~D_2_qn : 1'bz;  // Controlled_Inverter controlled_inverter_3
  D_Flip_Flop #(.trigger("falling")) D_3 (
    .clk(not_1_out), .D(D3), .Qn(D_3_qn), .preset(1'b0), .en(1'b1), .reset(1'b0));  // open: Q
  assign Q3 = not_2_out ? ~D_3_qn : 1'bz;  // Controlled_Inverter controlled_inverter_4
  D_Flip_Flop #(.trigger("falling")) D_4 (
    .clk(not_1_out), .D(D4), .Qn(D_4_qn), .preset(1'b0), .en(1'b1), .reset(1'b0));  // open: Q
  assign Q4 = not_2_out ? ~D_4_qn : 1'bz;  // Controlled_Inverter controlled_inverter_5
  D_Flip_Flop #(.trigger("falling")) D_5 (
    .clk(not_1_out), .D(D5), .Qn(D_5_qn), .preset(1'b0), .en(1'b1), .reset(1'b0));  // open: Q
  assign Q5 = not_2_out ? ~D_5_qn : 1'bz;  // Controlled_Inverter controlled_inverter_6
  D_Flip_Flop #(.trigger("falling")) D_6 (
    .clk(not_1_out), .D(D6), .Qn(D_6_qn), .preset(1'b0), .en(1'b1), .reset(1'b0));  // open: Q
  assign Q6 = not_2_out ? ~D_6_qn : 1'bz;  // Controlled_Inverter controlled_inverter_7
  D_Flip_Flop #(.trigger("falling")) D_7 (.clk(not_1_out), .D(D7), .Qn(D_7_qn), .en(1'b1));  // open: Q, preset, reset
  assign Q7 = not_2_out ? ~D_7_qn : 1'bz;  // Controlled_Inverter controlled_inverter_8

  // Notes on the sheet:
  //   74F374 8 * D-flip-flop
endmodule
