// Logisim project 74hc139 test.circ as structural Verilog: 1 circuit, main circuit main
module main (
  input  in_1,
  input  in_2,
  input  in_3,
  input  in_4,
  input  in_5,
  input  in_6
);

  wire n74hc139_1_n1y0, n74hc139_1_n1y1, n74hc139_1_n1y2, n74hc139_1_n1y3, n74hc139_1_n2y0, n74hc139_1_n2y1,
       n74hc139_1_n2y2, n74hc139_1_n2y3;

  _74hc139 u_74hc139_1 (
    ._1a0(in_1), ._1a1(in_2), .n1e(in_3), ._2a0(in_4), ._2a1(in_5), .n2e(in_6), .n1y0(n74hc139_1_n1y0),
    .n1y1(n74hc139_1_n1y1), .n1y2(n74hc139_1_n1y2), .n1y3(n74hc139_1_n1y3), .n2y0(n74hc139_1_n2y0),
    .n2y1(n74hc139_1_n2y1), .n2y2(n74hc139_1_n2y2), .n2y3(n74hc139_1_n2y3));
  LED led_1 (.in(n74hc139_1_n1y0));
  LED led_2 (.in(n74hc139_1_n1y1));
  LED led_3 (.in(n74hc139_1_n1y2));
  LED led_4 (.in(n74hc139_1_n1y3));
  LED led_5 (.in(n74hc139_1_n2y0));
  LED led_6 (.in(n74hc139_1_n2y1));
  LED led_7 (.in(n74hc139_1_n2y2));
  LED led_8 (.in(n74hc139_1_n2y3));
endmodule
