// Logisim project 74hc139.circ as structural Verilog: 2 circuits, main circuit 74hc139
module _74hc139 (
  input  _1a0,
  input  _1a1,
  input  n1e,
  input  _2a0,
  input  _2a1,
  input  n2e,
  output n1y0,
  output n1y1,
  output n1y2,
  output n1y3,
  output n2y0,
  output n2y1,
  output n2y2,
  output n2y3
);

  _74hc139_demux u_74hc139_demux_1 (.a0(_1a0), .a1(_1a1), .ne(n1e), .ny0(n1y0), .ny1(n1y1), .ny2(n1y2), .ny3(n1y3));
  _74hc139_demux u_74hc139_demux_2 (.a0(_2a0), .a1(_2a1), .ne(n2e), .ny0(n2y0), .ny1(n2y1), .ny2(n2y2), .ny3(n2y3));

  // Notes on the sheet:
  //   74HC139 dual 2- to 4-line decoder/demultiplexer
endmodule

module _74hc139_demux (
  input  a0,
  input  a1,
  input  ne,
  output ny0,
  output ny1,
  output ny2,
  output ny3
);

  wire not_1_out, not_2_out, not_3_out, not_4_out, not_5_out;

  not not_1 (not_1_out, a0);
  not not_2 (not_2_out, a1);
  not not_3 (not_3_out, ne);
  not not_4 (not_4_out, not_1_out);
  not not_5 (not_5_out, not_2_out);
  nand nand_1 (ny0, not_1_out, not_2_out, not_3_out);
  nand nand_2 (ny1, not_4_out, not_2_out, not_3_out);
  nand nand_3 (ny2, not_1_out, not_5_out, not_3_out);
  nand nand_4 (ny3, not_4_out, not_5_out, not_3_out);
endmodule
