// Logisim project 74hc164 test.circ as structural Verilog: 1 circuit, main circuit main
module main (
  input  in_1,
  input  in_2,
  input  in_3
);

  wire button_1_out, n74hc164_1_q0, n74hc164_1_q1, n74hc164_1_q2, n74hc164_1_q3, n74hc164_1_q4,
       n74hc164_1_q5, n74hc164_1_q6, n74hc164_1_q7;

  Button button_1 (.out(button_1_out));
  _74hc164 u_74hc164_1 (
    .dsa(in_1), .dsb(in_2), .cp(button_1_out), .nmr(in_3), .q0(n74hc164_1_q0), .q1(n74hc164_1_q1),
    .q2(n74hc164_1_q2), .q3(n74hc164_1_q3), .q4(n74hc164_1_q4), .q5(n74hc164_1_q5), .q6(n74hc164_1_q6),
    .q7(n74hc164_1_q7));
  DotMatrix #(.inputtype("row"), .matrixcols(1), .matrixrows(8), .dotshape("circle")) dotmatrix_1 (
    .row0(n74hc164_1_q0), .row1(n74hc164_1_q1), .row2(n74hc164_1_q2), .row3(n74hc164_1_q3),
    .row4(n74hc164_1_q4), .row5(n74hc164_1_q5), .row6(n74hc164_1_q6), .row7(n74hc164_1_q7));
endmodule
