// Logisim project 74hc164.circ as structural Verilog: 1 circuit, main circuit 74hc164
module _74hc164 (
  input  dsa,
  input  dsb,
  input  cp,
  input  nmr,
  output q0,
  output q1,
  output q2,
  output q3,
  output q4,
  output q5,
  output q6,
  output q7
);

  wire and_1_out, not_1_out;

  and and_1 (and_1_out, dsa, dsb);
  not not_1 (not_1_out, nmr);
  D_Flip_Flop d_ff_1 (.clk(cp), .D(and_1_out), .Q(q0), .preset(1'b0), .en(1'b1), .reset(not_1_out));  // open: Qn
  D_Flip_Flop d_ff_2 (.clk(cp), .D(q0), .Q(q1), .preset(1'b0), .en(1'b1), .reset(not_1_out));  // open: Qn
  D_Flip_Flop d_ff_3 (.clk(cp), .D(q1), .Q(q2), .preset(1'b0), .en(1'b1), .reset(not_1_out));  // open: Qn
  D_Flip_Flop d_ff_4 (.clk(cp), .D(q2), .Q(q3), .preset(1'b0), .en(1'b1), .reset(not_1_out));  // open: Qn
  D_Flip_Flop d_ff_5 (.clk(cp), .D(q3), .Q(q4), .preset(1'b0), .en(1'b1), .reset(not_1_out));  // open: Qn
  D_Flip_Flop d_ff_6 (.clk(cp), .D(q4), .Q(q5), .preset(1'b0), .en(1'b1), .reset(not_1_out));  // open: Qn
  D_Flip_Flop d_ff_7 (.clk(cp), .D(q5), .Q(q6), .preset(1'b0), .en(1'b1), .reset(not_1_out));  // open: Qn
  D_Flip_Flop d_ff_8 (.clk(cp), .D(q6), .Q(q7), .preset(1'b0), .en(1'b1), .reset(not_1_out));  // open: Qn

  // Notes on the sheet:
  //   74HC164 / 74HCT164, 8-bit serial-in, parallel-out shift register
endmodule
