// Logisim project 74hc166 test.circ as structural Verilog: 1 circuit, main circuit main
module main (
  input  in_1,
  input  in_2,
  input  in_3,
  input  in_4,
  input  in_5,
  input  in_6,
  input  in_7,
  input  in_8,
  input  in_9,
  input  in_10,
  input  in_11,
  input  in_12
);

  wire button_1_out, n74hc166_1_q_h;

  Button button_1 (.out(button_1_out));
  _74hc166 u_74hc166_1 (
    .SH_nLD(in_1), .SER(in_2), .CLK_INH(in_3), .CLK(button_1_out), .nCLR(in_4), .Q_h(n74hc166_1_q_h),
    .A(in_5), .B(in_6), .C(in_7), .D(in_8), .E(in_9), .F(in_10), .G(in_11), .H(in_12));
  LED led_1 (.in(n74hc166_1_q_h));
endmodule
