// Logisim project 74hc166.circ as structural Verilog: 1 circuit, main circuit 74hc166
module _74hc166 (
  input  A,
  input  B,
  input  C,
  input  D,
  input  E,
  input  F,
  input  G,
  input  H,
  input  SH_nLD,
  input  SER,
  input  CLK_INH,
  input  CLK,
  input  nCLR,
  output Q_h
);

  wire and_1_out, and_2_out, and_3_out, and_4_out, and_5_out, and_6_out, and_7_out, and_8_out, and_9_out,
       and_10_out, and_11_out, and_12_out, and_13_out, and_14_out, and_15_out, and_16_out, d_ff_1_q,
       d_ff_2_q, d_ff_3_q, d_ff_4_q, d_ff_5_q, d_ff_6_q, d_ff_7_q, not_1_out, not_2_out, not_3_out, or_1_out,
       or_2_out, or_3_out, or_4_out, or_5_out, or_6_out, or_7_out, or_8_out, or_9_out;

  not not_1 (not_1_out, SH_nLD);
  not not_2 (not_2_out, not_1_out);
  and and_1 (and_1_out, SER, not_2_out);
  or or_1 (or_1_out, and_1_out, and_2_out);
  or or_2 (or_2_out, CLK_INH, CLK);
  not not_3 (not_3_out, nCLR);
  and and_2 (and_2_out, not_1_out, A);
  and and_3 (and_3_out, d_ff_1_q, not_2_out);
  D_Flip_Flop d_ff_1 (.clk(or_2_out), .D(or_1_out), .Q(d_ff_1_q), .reset(not_3_out));  // open: Qn, preset, en
  and and_4 (and_4_out, not_1_out, B);
  or or_3 (or_3_out, and_3_out, and_4_out);
  D_Flip_Flop d_ff_2 (.clk(or_2_out), .D(or_3_out), .Q(d_ff_2_q), .reset(not_3_out));  // open: Qn, preset, en
  and and_5 (and_5_out, not_1_out, C);
  and and_6 (and_6_out, d_ff_2_q, not_2_out);
  or or_4 (or_4_out, and_6_out, and_5_out);
  D_Flip_Flop d_ff_3 (.clk(or_2_out), .D(or_4_out), .Q(d_ff_3_q), .reset(not_3_out));  // open: Qn, preset, en
  and and_7 (and_7_out, not_1_out, D);
  and and_8 (and_8_out, d_ff_3_q, not_2_out);
  or or_5 (or_5_out, and_8_out, and_7_out);
  and and_9 (and_9_out, d_ff_4_q, not_2_out);
  or or_6 (or_6_out, and_9_out, and_11_out);
  D_Flip_Flop d_ff_4 (.clk(or_2_out), .D(or_5_out), .Q(d_ff_4_q), .reset(not_3_out));  // open: Qn, preset, en
  and and_10 (and_10_out, d_ff_5_q, not_2_out);
  and and_11 (and_11_out, not_1_out, E);
  D_Flip_Flop d_ff_5 (.clk(or_2_out), .D(or_6_out), .Q(d_ff_5_q), .reset(not_3_out));  // open: Qn, preset, en
  and and_12 (and_12_out, not_1_out, F);
  or or_7 (or_7_out, and_10_out, and_12_out);
  D_Flip_Flop d_ff_6 (.clk(or_2_out), .D(or_7_out), .Q(d_ff_6_q), .reset(not_3_out));  // open: Qn, preset, en
  and and_13 (and_13_out, d_ff_6_q, not_2_out);
  and and_14 (and_14_out, not_1_out, G);
  or or_8 (or_8_out, and_13_out, and_14_out);
  D_Flip_Flop d_ff_7 (.clk(or_2_out), .D(or_8_out), .Q(d_ff_7_q), .reset(not_3_out));  // open: Qn, preset, en
  and and_15 (and_15_out, not_1_out, H);
  and and_16 (and_16_out, d_ff_7_q, not_2_out);
  or or_9 (or_9_out, and_16_out, and_15_out);
  D_Flip_Flop d_ff_8 (.clk(or_2_out), .D(or_9_out), .Q(Q_h), .reset(not_3_out));  // open: Qn, preset, en

  // Notes on the sheet:
  //   74HC166: 8-bit parallel-load shift register
endmodule
