// Logisim project 74hc194 test.circ as structural Verilog: 1 circuit, main circuit main
module main (
  input  in_1,
  input  in_2,
  input  in_3,
  input  in_4,
  input  in_5,
  input  in_6,
  input  in_7,
  input  in_8,
  input  in_9,
  output out_10,
  output out_11,
  output out_12,
  output out_13
);

  wire button_1_out;

  Button button_1 (.out(button_1_out));
  _74hc194 u_74hc194_1 (
    .S1(in_1), .S0(in_2), .DSR(in_3), .DSL(in_4), .CP(button_1_out), .nMR(in_5), .Q0(out_10), .Q1(out_11),
    .Q2(out_12), .Q3(out_13), .D0(in_6), .D1(in_7), .D2(in_8), .D3(in_9));
endmodule
