// Logisim project 74hc194.circ as structural Verilog: 1 circuit, main circuit 74hc194
module _74hc194 (
  input  D0,
  input  D1,
  input  D2,
  input  D3,
  input  S1,
  input  S0,
  input  DSR,
  input  DSL,
  input  CP,
  input  nMR,
  output Q0,
  output Q1,
  output Q2,
  output Q3
);

  wire b0_qn, b1_qn, b2_qn, b3_qn, nand_1_out, nand_2_out, nand_3_out, nand_4_out, nand_5_out, nand_6_out,
       nand_7_out, nand_8_out, nand_9_out, nand_10_out, nand_11_out, nand_12_out, nand_13_out, nand_14_out,
       nand_15_out, nand_16_out, nand_17_out, nand_18_out, nand_19_out, nand_20_out, not_1_out, not_2_out,
       not_3_out, not_4_out, not_5_out, not_6_out, not_7_out, not_8_out, not_9_out;

  not not_1 (not_1_out, S1);
  not not_2 (not_2_out, not_1_out);
  not not_3 (not_3_out, S0);
  not not_4 (not_4_out, not_3_out);
  nand nand_1 (nand_1_out, ~DSR, not_1_out, not_4_out);  // NAND_Gate
  not not_5 (not_5_out, nMR);
  nand nand_2 (nand_2_out, not_3_out, not_1_out, b0_qn);
  nand nand_3 (nand_3_out, not_4_out, not_2_out, ~D0);  // NAND_Gate
  nand nand_4 (nand_4_out, not_3_out, not_2_out, b1_qn);
  nand nand_5 (nand_5_out, nand_1_out, nand_3_out, nand_4_out, nand_2_out);
  not not_6 (not_6_out, nand_5_out);
  D_Flip_Flop b0 (.clk(CP), .D(not_6_out), .Q(Q0), .Qn(b0_qn), .reset(not_5_out));  // open: preset, en
  nand nand_6 (nand_6_out, not_3_out, not_2_out, b2_qn);
  nand nand_7 (nand_7_out, not_4_out, not_2_out, ~D1);  // NAND_Gate
  nand nand_8 (nand_8_out, b0_qn, not_1_out, not_4_out);
  nand nand_9 (nand_9_out, nand_8_out, nand_7_out, nand_6_out, nand_10_out);
  not not_7 (not_7_out, nand_9_out);
  nand nand_10 (nand_10_out, not_3_out, not_1_out, b1_qn);
  D_Flip_Flop b1 (.clk(CP), .D(not_7_out), .Q(Q1), .Qn(b1_qn), .reset(not_5_out));  // open: preset, en
  nand nand_11 (nand_11_out, b1_qn, not_1_out, not_4_out);
  nand nand_12 (nand_12_out, not_4_out, not_2_out, ~D2);  // NAND_Gate
  nand nand_13 (nand_13_out, nand_11_out, nand_12_out, nand_14_out, nand_15_out);
  not not_8 (not_8_out, nand_13_out);
  nand nand_14 (nand_14_out, not_3_out, not_2_out, b3_qn);
  nand nand_15 (nand_15_out, not_3_out, not_1_out, b2_qn);
  nand nand_16 (nand_16_out, b2_qn, not_1_out, not_4_out);
  nand nand_17 (nand_17_out, not_4_out, not_2_out, ~D3);  // NAND_Gate
  D_Flip_Flop b2 (.clk(CP), .D(not_8_out), .Q(Q2), .Qn(b2_qn), .reset(not_5_out));  // open: preset, en
  nand nand_18 (nand_18_out, not_3_out, not_2_out, ~DSL);  // NAND_Gate
  nand nand_19 (nand_19_out, not_3_out, not_1_out, b3_qn);
  nand nand_20 (nand_20_out, nand_16_out, nand_17_out, nand_18_out, nand_19_out);
  not not_9 (not_9_out, nand_20_out);
  D_Flip_Flop b3 (.clk(CP), .D(not_9_out), .Q(Q3), .Qn(b3_qn), .reset(not_5_out));  // open: preset, en

  // Notes on the sheet:
  //   74HC194, 4-bit bidirectional universal shift register
endmodule
