// Logisim project 74hc259 test.circ as structural Verilog: 1 circuit, main circuit main
module main (
  input  in_1,
  input  in_2,
  input  in_3,
  input  in_4,
  input  in_5,
  input  in_6
);

  wire n74hc259_1_q0, n74hc259_1_q1, n74hc259_1_q2, n74hc259_1_q3, n74hc259_1_q4, n74hc259_1_q5,
       n74hc259_1_q6, n74hc259_1_q7;

  _74hc259 u_74hc259_1 (
    .nLE(in_1), .D(in_2), .A0(in_3), .A1(in_4), .A2(in_5), .nMR(in_6), .Q0(n74hc259_1_q0),
    .Q1(n74hc259_1_q1), .Q2(n74hc259_1_q2), .Q3(n74hc259_1_q3), .Q4(n74hc259_1_q4), .Q5(n74hc259_1_q5),
    .Q6(n74hc259_1_q6), .Q7(n74hc259_1_q7));
  LED led_1 (.in(n74hc259_1_q0));
  LED led_2 (.in(n74hc259_1_q1));
  LED led_3 (.in(n74hc259_1_q2));
  LED led_4 (.in(n74hc259_1_q3));
  LED led_5 (.in(n74hc259_1_q4));
  LED led_6 (.in(n74hc259_1_q5));
  LED led_7 (.in(n74hc259_1_q6));
  LED led_8 (.in(n74hc259_1_q7));
endmodule
