// Logisim project 74hc259.circ as structural Verilog: 2 circuits, main circuit 74hc259
module _74hc259 (
  input  nLE,
  input  D,
  input  A0,
  input  A1,
  input  A2,
  input  nMR,
  output Q0,
  output Q1,
  output Q2,
  output Q3,
  output Q4,
  output Q5,
  output Q6,
  output Q7
);

  wire nor_1_out, nor_2_out, not_1_out, not_2_out, not_3_out, not_4_out, not_5_out, not_6_out;

  not not_1 (not_1_out, A0);
  not not_2 (not_2_out, A1);
  not not_3 (not_3_out, A2);
  nor nor_1 (nor_1_out, nLE, D);
  not not_4 (not_4_out, not_1_out);
  not not_5 (not_5_out, not_2_out);
  not not_6 (not_6_out, not_3_out);
  nor nor_2 (nor_2_out, nLE, nor_1_out);
  _74hc259_latch u_74hc259_latch_1 (
    .x0(nor_1_out), .x1(not_1_out), .x2(not_2_out), .x3(not_3_out), .y4(nMR), .z0(nor_2_out), .z1(not_1_out),
    .z2(not_2_out), .z3(not_3_out), .Q(Q0));
  _74hc259_latch u_74hc259_latch_2 (
    .x0(nor_1_out), .x1(not_4_out), .x2(not_2_out), .x3(not_3_out), .y4(nMR), .z0(nor_2_out), .z1(not_4_out),
    .z2(not_2_out), .z3(not_3_out), .Q(Q1));
  _74hc259_latch u_74hc259_latch_3 (
    .x0(not_1_out), .x1(not_5_out), .x2(nor_1_out), .x3(not_3_out), .y4(nMR), .z0(nor_2_out), .z1(not_1_out),
    .z2(not_5_out), .z3(not_3_out), .Q(Q2));
  _74hc259_latch u_74hc259_latch_4 (
    .x0(nor_1_out), .x1(not_4_out), .x2(not_5_out), .x3(not_3_out), .y4(nMR), .z0(nor_2_out), .z1(not_4_out),
    .z2(not_5_out), .z3(not_3_out), .Q(Q3));
  _74hc259_latch u_74hc259_latch_5 (
    .x0(not_1_out), .x1(not_2_out), .x2(not_6_out), .x3(nor_1_out), .y4(nMR), .z0(not_1_out), .z1(not_2_out),
    .z2(not_6_out), .z3(nor_2_out), .Q(Q4));
  _74hc259_latch u_74hc259_latch_6 (
    .x0(not_4_out), .x1(not_2_out), .x2(not_6_out), .x3(nor_1_out), .y4(nMR), .z0(not_4_out), .z1(not_2_out),
    .z2(not_6_out), .z3(nor_2_out), .Q(Q5));
  _74hc259_latch u_74hc259_latch_7 (
    .x0(not_1_out), .x1(not_5_out), .x2(not_6_out), .x3(nor_1_out), .y4(nMR), .z0(not_1_out), .z1(not_5_out),
    .z2(not_6_out), .z3(nor_2_out), .Q(Q6));
  _74hc259_latch u_74hc259_latch_8 (
    .x0(not_4_out), .x1(not_5_out), .x2(not_6_out), .x3(nor_1_out), .y4(nMR), .z0(not_4_out), .z1(not_5_out),
    .z2(not_6_out), .z3(nor_2_out), .Q(Q7));

  // Notes on the sheet:
  //   74HC259 8-bit addressable latch
endmodule

module _74hc259_latch (
  input  x0,
  input  x1,
  input  x2,
  input  x3,
  input  y4,
  input  z0,
  input  z1,
  input  z2,
  input  z3,
  output Q
);

  wire and_1_out, and_2_out, and_3_out, nor_2_out;

  and and_1 (and_1_out, x0, x1, x2, x3);
  and and_2 (and_2_out, Q, y4);
  and and_3 (and_3_out, z0, z1, z2, z3);
  nor nor_1 (Q, and_1_out, nor_2_out);
  nor nor_2 (nor_2_out, and_2_out, and_3_out);
endmodule
