// Logisim project 74hc42 test.circ as structural Verilog: 1 circuit, main circuit main
module main (
  input  in_1,
  input  in_2,
  input  in_3,
  input  in_4
);

  wire n74hc42_1_n0y, n74hc42_1_n1y, n74hc42_1_n2y, n74hc42_1_n3y, n74hc42_1_n4y, n74hc42_1_n5y,
       n74hc42_1_n6y, n74hc42_1_n7y, n74hc42_1_n8y, n74hc42_1_n9y;

  _74hc42 u_74hc42_1 (
    ._0A(in_1), ._1A(in_2), ._2A(in_3), ._3A(in_4), .n0Y(n74hc42_1_n0y), .n1Y(n74hc42_1_n1y),
    .n2Y(n74hc42_1_n2y), .n3Y(n74hc42_1_n3y), .n4Y(n74hc42_1_n4y), .n5Y(n74hc42_1_n5y), .n6Y(n74hc42_1_n6y),
    .n7Y(n74hc42_1_n7y), .n8Y(n74hc42_1_n8y), .n9Y(n74hc42_1_n9y));
  LED led_1 (.in(n74hc42_1_n0y));
  LED led_2 (.in(n74hc42_1_n1y));
  LED led_3 (.in(n74hc42_1_n2y));
  LED led_4 (.in(n74hc42_1_n3y));
  LED led_5 (.in(n74hc42_1_n4y));
  LED led_6 (.in(n74hc42_1_n5y));
  LED led_7 (.in(n74hc42_1_n6y));
  LED led_8 (.in(n74hc42_1_n7y));
  LED led_9 (.in(n74hc42_1_n8y));
  LED led_10 (.in(n74hc42_1_n9y));
endmodule
