// Logisim project 74hc42.circ as structural Verilog: 1 circuit, main circuit 74hc42
module _74hc42 (
  input  _0A,
  input  _1A,
  input  _2A,
  input  _3A,
  output n0Y,
  output n1Y,
  output n2Y,
  output n3Y,
  output n4Y,
  output n5Y,
  output n6Y,
  output n7Y,
  output n8Y,
  output n9Y
);

  wire and_1_out, and_2_out, and_3_out, and_4_out, and_5_out, and_6_out, and_7_out, and_8_out, and_9_out,
       and_10_out, nand_1_out, nand_2_out, nand_3_out, nand_4_out, nand_5_out, nand_6_out, nand_7_out,
       not_1_out, not_2_out, not_3_out, not_4_out, not_5_out, not_6_out, not_7_out, not_8_out;

  not not_1 (not_1_out, _0A);
  not not_2 (not_2_out, _1A);
  not not_3 (not_3_out, _2A);
  not not_4 (not_4_out, _3A);
  not not_5 (not_5_out, not_1_out);
  not not_6 (not_6_out, not_2_out);
  not not_7 (not_7_out, not_3_out);
  not not_8 (not_8_out, not_4_out);
  nand nand_1 (nand_1_out, not_1_out, not_2_out);
  nand nand_2 (nand_2_out, not_5_out, not_2_out);
  nand nand_3 (nand_3_out, not_1_out, not_6_out);
  nand nand_4 (nand_4_out, not_5_out, not_6_out);
  nand nand_5 (nand_5_out, not_3_out, not_4_out);
  nand nand_6 (nand_6_out, not_7_out, not_4_out);
  nand nand_7 (nand_7_out, not_3_out, not_8_out);
  and and_1 (and_1_out, ~nand_1_out, ~nand_5_out);  // AND_Gate
  and and_2 (and_2_out, ~nand_2_out, ~nand_5_out);  // AND_Gate
  and and_3 (and_3_out, ~nand_3_out, ~nand_5_out);  // AND_Gate
  and and_4 (and_4_out, ~nand_4_out, ~nand_5_out);  // AND_Gate
  and and_5 (and_5_out, ~nand_1_out, ~nand_6_out);  // AND_Gate
  and and_6 (and_6_out, ~nand_2_out, ~nand_6_out);  // AND_Gate
  and and_7 (and_7_out, ~nand_3_out, ~nand_6_out);  // AND_Gate
  and and_8 (and_8_out, ~nand_4_out, ~nand_6_out);  // AND_Gate
  and and_9 (and_9_out, ~nand_1_out, ~nand_7_out);  // AND_Gate
  and and_10 (and_10_out, ~nand_2_out, ~nand_7_out);  // AND_Gate
  not not_9 (n0Y, and_1_out);
  not not_10 (n1Y, and_2_out);
  not not_11 (n2Y, and_3_out);
  not not_12 (n3Y, and_4_out);
  not not_13 (n4Y, and_5_out);
  not not_14 (n5Y, and_6_out);
  not not_15 (n6Y, and_7_out);
  not not_16 (n7Y, and_8_out);
  not not_17 (n8Y, and_9_out);
  not not_18 (n9Y, and_10_out);

  // Notes on the sheet:
  //   74HC42 BCD to decimal decoder
endmodule
