// Logisim project 74hc74 test.circ as structural Verilog: 1 circuit, main circuit main
module main (
  input  in_1,
  input  in_2,
  input  in_3,
  input  in_4,
  input  in_5,
  input  in_6,
  input  in_7,
  input  in_8,
  output out_9,
  output out_10,
  output out_11,
  output out_12
);

  _74hc74 u_74hc74_1 (
    .n1set(in_1), ._1clk(in_2), ._1d(in_3), .n1res(in_4), .n2set(in_5), ._2clk(in_6), ._2d(in_7),
    .n2res(in_8), ._1q(out_9), .n1q(out_10), ._2q(out_11), .n2q(out_12));
endmodule
