// Logisim project 74hc74.circ as structural Verilog: 1 circuit, main circuit 74hc74
module _74hc74 (
  input  n1set,
  input  _1clk,
  input  _1d,
  input  n1res,
  input  n2set,
  input  _2clk,
  input  _2d,
  input  n2res,
  output _1q,
  output n1q,
  output _2q,
  output n2q
);

  wire and_1_out, and_2_out, d_ff_1_q, d_ff_1_qn, d_ff_2_q, d_ff_2_qn, not_1_out, not_2_out, not_3_out,
       not_4_out;

  not not_1 (not_1_out, n1set);
  not not_2 (not_2_out, n1res);
  not not_3 (not_3_out, n2set);
  not not_4 (not_4_out, n2res);
  D_Flip_Flop d_ff_1 (
    .clk(_1clk), .D(_1d), .Q(d_ff_1_q), .Qn(d_ff_1_qn), .preset(not_1_out), .reset(not_2_out));  // open: en
  D_Flip_Flop d_ff_2 (
    .clk(_2clk), .D(_2d), .Q(d_ff_2_q), .Qn(d_ff_2_qn), .preset(not_3_out), .reset(not_4_out));  // open: en
  and and_1 (and_1_out, not_1_out, not_2_out);
  and and_2 (and_2_out, not_3_out, not_4_out);
  or or_1 (_1q, and_1_out, d_ff_1_q);
  or or_2 (n1q, and_1_out, d_ff_1_qn);
  or or_3 (_2q, and_2_out, d_ff_2_q);
  or or_4 (n2q, and_2_out, d_ff_2_qn);

  // Notes on the sheet:
  //   74 HC 74: dual D-type flip-flip with asynchronous set/reset
endmodule
