// Logisim project 74ls156 test.circ as structural Verilog: 1 circuit, main circuit main
module main (
  input  in_1,
  input  in_2,
  input  in_3,
  input  in_4,
  input  in_5,
  input  in_6
);

  wire n74ls156_1_q0a_prime, n74ls156_1_q0b_prime, n74ls156_1_q1a_prime, n74ls156_1_q1b_prime,
       n74ls156_1_q2a_prime, n74ls156_1_q3a_prime, n74ls156_1_q3b_prime, n74ls156_1_q4b_prime;

  _74ls156 u_74ls156_1 (
    .Eb1_prime(in_3), .Eb2_prime(in_4), .A0(in_5), .A1(in_6), .Ea1_prime(in_1), .Ea2(in_2),
    .Q4b_prime(n74ls156_1_q4b_prime), .Q3b_prime(n74ls156_1_q3b_prime), .Q1b_prime(n74ls156_1_q1b_prime),
    .Q0b_prime(n74ls156_1_q0b_prime), .Q3a_prime(n74ls156_1_q3a_prime), .Q2a_prime(n74ls156_1_q2a_prime),
    .Q1a_prime(n74ls156_1_q1a_prime), .Q0a_prime(n74ls156_1_q0a_prime));
  LED led_1 (.in(n74ls156_1_q4b_prime));
  LED led_2 (.in(n74ls156_1_q3b_prime));
  LED led_3 (.in(n74ls156_1_q1b_prime));
  LED led_4 (.in(n74ls156_1_q0b_prime));
  LED led_5 (.in(n74ls156_1_q3a_prime));
  LED led_6 (.in(n74ls156_1_q2a_prime));
  LED led_7 (.in(n74ls156_1_q1a_prime));
  LED led_8 (.in(n74ls156_1_q0a_prime));
endmodule
