// Logisim project 74ls156.circ as structural Verilog: 1 circuit, main circuit 74ls156
module _74ls156 (
  input  Eb1_prime,
  input  Eb2_prime,
  input  A0,
  input  A1,
  input  Ea1_prime,
  input  Ea2,
  output Q4b_prime,
  output Q3b_prime,
  output Q1b_prime,
  output Q0b_prime,
  output Q3a_prime,
  output Q2a_prime,
  output Q1a_prime,
  output Q0a_prime
);

  wire and_1_out, and_2_out, not_1_out, not_2_out, not_3_out, not_4_out;

  not not_1 (not_1_out, A0);
  not not_2 (not_2_out, A1);
  and and_1 (and_1_out, ~Ea1_prime, Ea2);  // AND_Gate
  and and_2 (and_2_out, ~Eb1_prime, ~Eb2_prime);  // AND_Gate
  not not_3 (not_3_out, not_1_out);
  not not_4 (not_4_out, not_2_out);
  nand _7 (Q4b_prime, not_4_out, not_3_out, and_2_out);
  nand _6 (Q3b_prime, not_4_out, not_1_out, and_2_out);
  nand _5 (Q1b_prime, not_3_out, not_2_out, and_2_out);
  nand _4 (Q0b_prime, and_2_out, not_2_out, not_1_out);
  nand _3 (Q3a_prime, not_4_out, not_3_out, and_1_out);
  nand _2 (Q2a_prime, not_4_out, not_1_out, and_1_out);
  nand _1 (Q1a_prime, not_3_out, not_2_out, and_1_out);
  nand _0 (Q0a_prime, and_1_out, not_2_out, not_1_out);

  // Notes on the sheet:
  //   74LS156 Dual 1-of-4 decoder/demultiplexer
endmodule
