// Logisim project cd4017 test.circ as structural Verilog: 1 circuit, main circuit main
module main (
  input  in_1,
  input  in_2
);

  wire button_1_out, cd4017_1_cout, cd4017_1_q0, cd4017_1_q1, cd4017_1_q2, cd4017_1_q3, cd4017_1_q4,
       cd4017_1_q5, cd4017_1_q6, cd4017_1_q7, cd4017_1_q8, cd4017_1_q9;

  Button button_1 (.out(button_1_out));
  cd4017 cd4017_1 (
    .reset(in_2), .clk(button_1_out), .nclk_en(in_1), .q0(cd4017_1_q0), .q1(cd4017_1_q1), .q2(cd4017_1_q2),
    .q3(cd4017_1_q3), .q4(cd4017_1_q4), .q5(cd4017_1_q5), .q6(cd4017_1_q6), .q7(cd4017_1_q7),
    .q8(cd4017_1_q8), .q9(cd4017_1_q9), .Cout(cd4017_1_cout));
  LED led_1 (.in(cd4017_1_q0));
  LED led_2 (.in(cd4017_1_q1));
  LED led_3 (.in(cd4017_1_q2));
  LED led_4 (.in(cd4017_1_q3));
  LED led_5 (.in(cd4017_1_q4));
  LED led_6 (.in(cd4017_1_q5));
  LED led_7 (.in(cd4017_1_q6));
  LED led_8 (.in(cd4017_1_q7));
  LED led_9 (.in(cd4017_1_q8));
  LED led_10 (.in(cd4017_1_q9));
  LED led_11 (.in(cd4017_1_cout));
endmodule
