// Logisim project cd4017.circ as structural Verilog: 1 circuit, main circuit cd4017
module cd4017 (
  input  reset,
  input  clk,
  input  nclk_en,
  output q0,
  output q1,
  output q2,
  output q3,
  output q4,
  output q5,
  output q6,
  output q7,
  output q8,
  output q9,
  output Cout
);

  wire and_1_out, d_ff_1_q, d_ff_1_qn, d_ff_2_q, d_ff_2_qn, d_ff_3_q, d_ff_3_qn, d_ff_4_q, d_ff_4_qn,
       d_ff_5_q, d_ff_5_qn, nor_1_out, nor_2_out, not_1_out;

  not not_1 (not_1_out, clk);
  D_Flip_Flop d_ff_1 (.clk(nor_1_out), .D(d_ff_5_qn), .Q(d_ff_1_q), .Qn(d_ff_1_qn), .reset(reset));  // open: preset, en
  nor nor_1 (nor_1_out, not_1_out, nclk_en);
  and and_1 (and_1_out, d_ff_3_qn, d_ff_1_qn);
  D_Flip_Flop d_ff_2 (.clk(nor_1_out), .D(d_ff_1_q), .Q(d_ff_2_q), .Qn(d_ff_2_qn), .reset(reset));  // open: preset, en
  nor nor_2 (nor_2_out, d_ff_2_qn, and_1_out);
  D_Flip_Flop d_ff_3 (.clk(nor_1_out), .D(nor_2_out), .Q(d_ff_3_q), .Qn(d_ff_3_qn), .reset(reset));  // open: preset, en
  D_Flip_Flop d_ff_4 (.clk(nor_1_out), .D(d_ff_3_q), .Q(d_ff_4_q), .Qn(d_ff_4_qn), .reset(reset));  // open: preset, en
  D_Flip_Flop d_ff_5 (.clk(nor_1_out), .D(d_ff_4_q), .Q(d_ff_5_q), .Qn(d_ff_5_qn), .reset(reset));  // open: preset, en
  and and_2 (q0, d_ff_5_qn, d_ff_1_qn);
  and and_3 (q1, d_ff_1_q, d_ff_2_qn);
  and and_4 (q2, d_ff_2_q, d_ff_3_qn);
  and and_5 (q3, d_ff_3_q, d_ff_4_qn);
  and and_6 (q4, d_ff_4_q, d_ff_5_qn);
  and and_7 (q5, d_ff_1_q, d_ff_5_q);
  and and_8 (q6, d_ff_1_qn, d_ff_2_q);
  and and_9 (q7, d_ff_2_qn, d_ff_3_q);
  and and_10 (q8, d_ff_3_qn, d_ff_4_q);
  and and_11 (q9, d_ff_4_qn, d_ff_5_q);
  not not_2 (Cout, d_ff_5_q);

  // Notes on the sheet:
  //   CD4017 Decade counter
endmodule
