// Logisim project cd40175 test.circ as structural Verilog: 1 circuit, main circuit main
module main (
  input  in_1,
  input  in_2,
  input  in_3,
  input  in_4,
  input  in_5
);

  wire button_1_out, cd40175_1_nq0, cd40175_1_nq1, cd40175_1_nq2, cd40175_1_nq3, cd40175_1_q0, cd40175_1_q1,
       cd40175_1_q2, cd40175_1_q3;

  Button button_1 (.out(button_1_out));
  cd40175 cd40175_1 (
    .d0(in_1), .d1(in_2), .d2(in_3), .d3(in_4), .cp(button_1_out), .nres(in_5), .q0(cd40175_1_q0),
    .nq0(cd40175_1_nq0), .q1(cd40175_1_q1), .nq1(cd40175_1_nq1), .q2(cd40175_1_q2), .nq2(cd40175_1_nq2),
    .q3(cd40175_1_q3), .nq3(cd40175_1_nq3));
  LED led_1 (.in(cd40175_1_q0));
  LED led_2 (.in(cd40175_1_nq0));
  LED led_3 (.in(cd40175_1_q1));
  LED led_4 (.in(cd40175_1_nq1));
  LED led_5 (.in(cd40175_1_q2));
  LED led_6 (.in(cd40175_1_nq2));
  LED led_7 (.in(cd40175_1_q3));
  LED led_8 (.in(cd40175_1_nq3));
endmodule
