// Logisim project cd40175.circ as structural Verilog: 1 circuit, main circuit cd40175
module cd40175 (
  input  d0,
  input  d1,
  input  d2,
  input  d3,
  input  cp,
  input  nres,
  output q0,
  output nq0,
  output q1,
  output nq1,
  output q2,
  output nq2,
  output q3,
  output nq3
);

  wire not_1_out;

  not not_1 (not_1_out, nres);
  D_Flip_Flop d_ff_1 (.clk(cp), .D(d0), .Q(q0), .Qn(nq0), .reset(not_1_out));  // open: preset, en
  D_Flip_Flop d_ff_2 (.clk(cp), .D(d1), .Q(q1), .Qn(nq1), .reset(not_1_out));  // open: preset, en
  D_Flip_Flop d_ff_3 (.clk(cp), .D(d2), .Q(q2), .Qn(nq2), .reset(not_1_out));  // open: preset, en
  D_Flip_Flop d_ff_4 (.clk(cp), .D(d3), .Q(q3), .Qn(nq3), .reset(not_1_out));  // open: preset, en

  // Notes on the sheet:
  //   CD40175, Quad D-type flip-flip with active-low reset
endmodule
