// Logisim project cd4021 test.circ as structural Verilog: 1 circuit, main circuit main
module main (
  input  in_1,
  input  in_2,
  input  in_3,
  input  in_4,
  input  in_5,
  input  in_6,
  input  in_7,
  input  in_8,
  input  in_9,
  input  in_10
);

  wire button_1_out, cd4021_1_q5, cd4021_1_q6, cd4021_1_q7;

  Button button_1 (.out(button_1_out));
  cd4021 cd4021_1 (
    .p_s(in_1), .clk(button_1_out), .ds(in_2), .p0(in_3), .p1(in_4), .p2(in_5), .p3(in_6), .p4(in_7),
    .p5(in_8), .p6(in_9), .p7(in_10), .q7(cd4021_1_q7), .q6(cd4021_1_q6), .q5(cd4021_1_q5));
  LED led_1 (.in(cd4021_1_q5));
  LED led_2 (.in(cd4021_1_q6));
  LED led_3 (.in(cd4021_1_q7));
endmodule
