// Logisim project cd4021.circ as structural Verilog: 2 circuits, main circuit cd4021
module cd4021 (
  input  p_s,
  input  clk,
  input  ds,
  input  p0,
  input  p1,
  input  p2,
  input  p3,
  input  p4,
  input  p5,
  input  p6,
  input  p7,
  output q7,
  output q6,
  output q5
);

  wire bit_en_1_r, bit_en_1_s, bit_en_2_r, bit_en_2_s, bit_en_3_r, bit_en_3_s, bit_en_4_r, bit_en_4_s,
       bit_en_5_r, bit_en_5_s, bit_en_6_r, bit_en_6_s, bit_en_7_r, bit_en_7_s, bit_en_8_r, bit_en_8_s, d0_q,
       d1_q, d2_q, d3_q, d4_q, nand_1_out, not_1_out, not_2_out;

  not not_1 (not_1_out, p_s);
  not not_2 (not_2_out, clk);
  nand nand_1 (nand_1_out, not_1_out, not_2_out);
  bit_en bit_en_1 (.en(p_s), .d(p0), .s(bit_en_1_s), .r(bit_en_1_r));
  bit_en bit_en_2 (.en(p_s), .d(p1), .s(bit_en_2_s), .r(bit_en_2_r));
  D_Flip_Flop d0 (.clk(nand_1_out), .D(ds), .Q(d0_q), .preset(bit_en_1_s), .reset(bit_en_1_r));  // open: Qn, en
  bit_en bit_en_3 (.en(p_s), .d(p2), .s(bit_en_3_s), .r(bit_en_3_r));
  D_Flip_Flop d1 (.clk(nand_1_out), .D(d0_q), .Q(d1_q), .preset(bit_en_2_s), .reset(bit_en_2_r));  // open: Qn, en
  bit_en bit_en_4 (.en(p_s), .d(p3), .s(bit_en_4_s), .r(bit_en_4_r));
  D_Flip_Flop d2 (.clk(nand_1_out), .D(d1_q), .Q(d2_q), .preset(bit_en_3_s), .reset(bit_en_3_r));  // open: Qn, en
  bit_en bit_en_5 (.en(p_s), .d(p4), .s(bit_en_5_s), .r(bit_en_5_r));
  D_Flip_Flop d3 (.clk(nand_1_out), .D(d2_q), .Q(d3_q), .preset(bit_en_4_s), .reset(bit_en_4_r));  // open: Qn, en
  bit_en bit_en_6 (.en(p_s), .d(p5), .s(bit_en_6_s), .r(bit_en_6_r));
  D_Flip_Flop d4 (.clk(nand_1_out), .D(d3_q), .Q(d4_q), .preset(bit_en_5_s), .reset(bit_en_5_r));  // open: Qn, en
  bit_en bit_en_7 (.en(p_s), .d(p6), .s(bit_en_7_s), .r(bit_en_7_r));
  D_Flip_Flop d5 (.clk(nand_1_out), .D(d4_q), .Q(q5), .preset(bit_en_6_s), .reset(bit_en_6_r));  // open: Qn, en
  bit_en bit_en_8 (.en(p_s), .d(p7), .s(bit_en_8_s), .r(bit_en_8_r));
  D_Flip_Flop d6 (.clk(nand_1_out), .D(q5), .Q(q6), .preset(bit_en_7_s), .reset(bit_en_7_r));  // open: Qn, en
  D_Flip_Flop d7 (.clk(nand_1_out), .D(q6), .Q(q7), .preset(bit_en_8_s), .reset(bit_en_8_r));  // open: Qn, en

  // Notes on the sheet:
  //   CD4021: 8-bit asynchronous shift register
  //   Asynchronous parallel input, serial output
endmodule

module bit_en (
  input  en,
  input  d,
  output s,
  output r
);

  wire not_1_out;

  not not_1 (not_1_out, d);
  and and_1 (s, en, d);
  and and_2 (r, en, not_1_out);
endmodule
