// Logisim project cd4053 test.circ as structural Verilog: 1 circuit, main circuit main
module main (
  input  in_1,
  input  in_2,
  input  in_3,
  input  in_4,
  input  in_5,
  input  in_6,
  input  in_7
);

  wire cd4053_1_y0a, cd4053_1_y0b, cd4053_1_y0c, cd4053_1_y1a, cd4053_1_y1b, cd4053_1_y1c;

  cd4053 cd4053_1 (
    .Za(in_1), .Zb(in_2), .Zc(in_3), .Sa(in_4), .Sb(in_5), .Sc(in_6), .Enable_prime(in_7),
    .Y1a(cd4053_1_y1a), .Y0a(cd4053_1_y0a), .Y1b(cd4053_1_y1b), .Y0b(cd4053_1_y0b), .Y1c(cd4053_1_y1c),
    .Y0c(cd4053_1_y0c));
  LED led_1 (.in(cd4053_1_y1a));
  LED led_2 (.in(cd4053_1_y0a));
  LED led_3 (.in(cd4053_1_y1b));
  LED led_4 (.in(cd4053_1_y0b));
  LED led_5 (.in(cd4053_1_y1c));
  LED led_6 (.in(cd4053_1_y0c));
endmodule
