// Logisim project cd4053.circ as structural Verilog: 1 circuit, main circuit cd4053
module cd4053 (
  input  Za,
  input  Zb,
  input  Zc,
  input  Sa,
  input  Sb,
  input  Sc,
  input  Enable_prime,
  output Y1a,
  output Y0a,
  output Y1b,
  output Y0b,
  output Y1c,
  output Y0c
);

  wire nor_1_out, nor_2_out, nor_3_out, nor_4_out, nor_5_out, nor_6_out, not_1_out, not_2_out, not_3_out,
       not_4_out, not_5_out, not_6_out, not_7_out, not_8_out, not_9_out;

  not not_1 (not_1_out, Sa);
  not not_2 (not_2_out, Sb);
  not not_3 (not_3_out, Sc);
  nor nor_1 (nor_1_out, not_1_out, Enable_prime);
  nor nor_2 (nor_2_out, Sa, Enable_prime);
  nor nor_3 (nor_3_out, not_2_out, Enable_prime);
  nor nor_4 (nor_4_out, Sb, Enable_prime);
  nor nor_5 (nor_5_out, not_3_out, Enable_prime);
  nor nor_6 (nor_6_out, Sc, Enable_prime);
  not not_4 (not_4_out, nor_1_out);
  not not_5 (not_5_out, nor_2_out);
  not not_6 (not_6_out, nor_3_out);
  not not_7 (not_7_out, nor_4_out);
  not not_8 (not_8_out, nor_5_out);
  not not_9 (not_9_out, nor_6_out);
  // Transmission_Gate #(.gate("br")) transmission_1: pin names not known; wires that end beside it: Za, nor_1_out, not_4_out, Y1a
  // Transmission_Gate #(.gate("br")) transmission_2: pin names not known; wires that end beside it: Za, nor_2_out, not_5_out, Y0a
  // Transmission_Gate #(.gate("br")) transmission_3: pin names not known; wires that end beside it: Zb, nor_3_out, not_6_out, Y1b
  // Transmission_Gate #(.gate("br")) transmission_4: pin names not known; wires that end beside it: Zb, nor_4_out, not_7_out, Y0b
  // Transmission_Gate #(.gate("br")) transmission_5: pin names not known; wires that end beside it: Zc, nor_5_out, not_8_out, Y1c
  // Transmission_Gate #(.gate("br")) transmission_6: pin names not known; wires that end beside it: Zc, nor_6_out, not_9_out, Y0c

  // Notes on the sheet:
  //   CD4053
  //   Triple 2-channel analogue multiplexer/demultiplexer
endmodule
