// Logisim project cd4099 test.circ as structural Verilog: 1 circuit, main circuit main
module main (
  input  in_1,
  input  in_2,
  input  in_3,
  input  in_4,
  input  in_5,
  input  in_6
);

  wire cd4099_1_q0, cd4099_1_q1, cd4099_1_q2, cd4099_1_q3, cd4099_1_q4, cd4099_1_q5, cd4099_1_q6, cd4099_1_q7;

  cd4099 cd4099_1 (
    .A0(in_1), .A1(in_2), .A2(in_3), .DATA(in_4), .WRITE_DISABLE(in_5), .RESET(in_6), .Q0(cd4099_1_q0),
    .Q1(cd4099_1_q1), .Q2(cd4099_1_q2), .Q3(cd4099_1_q3), .Q4(cd4099_1_q4), .Q5(cd4099_1_q5),
    .Q6(cd4099_1_q6), .Q7(cd4099_1_q7));
  LED led_1 (.in(cd4099_1_q0));
  LED led_2 (.in(cd4099_1_q1));
  LED led_3 (.in(cd4099_1_q2));
  LED led_4 (.in(cd4099_1_q3));
  LED led_5 (.in(cd4099_1_q4));
  LED led_6 (.in(cd4099_1_q5));
  LED led_7 (.in(cd4099_1_q6));
  LED led_8 (.in(cd4099_1_q7));
endmodule
