// Logisim project cd4099.circ as structural Verilog: 4 circuits, main circuit cd4099
module cd4099 (
  input  A0,
  input  A1,
  input  A2,
  input  DATA,
  input  WRITE_DISABLE,
  input  RESET,
  output Q0,
  output Q1,
  output Q2,
  output Q3,
  output Q4,
  output Q5,
  output Q6,
  output Q7
);

  wire cd4099_adrdec_1_a0_2, cd4099_adrdec_1_a1_2, cd4099_adrdec_1_a2_2, cd4099_adrdec_1_d,
       cd4099_adrdec_1_na0, cd4099_adrdec_1_na1, cd4099_adrdec_1_na2, cd4099_adrdec_1_r, cd4099_adrdec_1_wd,
       cd4099_sreset_1_q, nand_1_out, nand_2_out, nand_3_out, nand_4_out, nand_5_out, nand_6_out, nand_7_out,
       nand_8_out, or_1_out;

  cd4099_sreset cd4099_sreset_1 (.Q(cd4099_sreset_1_q));
  cd4099_adrdec cd4099_adrdec_1 (
    .A0(A0), .A1(A1), .A2(A2), .DATA(DATA), .WRITE_DISABLE(WRITE_DISABLE), .RESET(RESET),
    .A0_2(cd4099_adrdec_1_a0_2), .nA0(cd4099_adrdec_1_na0), .A1_2(cd4099_adrdec_1_a1_2),
    .nA1(cd4099_adrdec_1_na1), .A2_2(cd4099_adrdec_1_a2_2), .nA2(cd4099_adrdec_1_na2), .D(cd4099_adrdec_1_d),
    .WD(cd4099_adrdec_1_wd), .R(cd4099_adrdec_1_r));
  or or_1 (or_1_out, cd4099_adrdec_1_r, cd4099_sreset_1_q);
  nand nand_1 (nand_1_out, cd4099_adrdec_1_na0, cd4099_adrdec_1_na1, cd4099_adrdec_1_na2);
  nand nand_2 (nand_2_out, cd4099_adrdec_1_a0_2, cd4099_adrdec_1_na1, cd4099_adrdec_1_na2);
  nand nand_3 (nand_3_out, cd4099_adrdec_1_na0, cd4099_adrdec_1_a1_2, cd4099_adrdec_1_na2);
  nand nand_4 (nand_4_out, cd4099_adrdec_1_a0_2, cd4099_adrdec_1_a1_2, cd4099_adrdec_1_na2);
  nand nand_5 (nand_5_out, cd4099_adrdec_1_na0, cd4099_adrdec_1_na1, cd4099_adrdec_1_a2_2);
  nand nand_6 (nand_6_out, cd4099_adrdec_1_a0_2, cd4099_adrdec_1_na1, cd4099_adrdec_1_a2_2);
  nand nand_7 (nand_7_out, cd4099_adrdec_1_na0, cd4099_adrdec_1_a1_2, cd4099_adrdec_1_a2_2);
  nand nand_8 (nand_8_out, cd4099_adrdec_1_a0_2, cd4099_adrdec_1_a1_2, cd4099_adrdec_1_a2_2);
  cd4099_latch cd4099_latch_1 (.R(or_1_out), .D(cd4099_adrdec_1_d), .WD(cd4099_adrdec_1_wd), .ZS(nand_1_out), .Q(Q0));
  cd4099_latch cd4099_latch_2 (.R(or_1_out), .D(cd4099_adrdec_1_d), .WD(cd4099_adrdec_1_wd), .ZS(nand_2_out), .Q(Q1));
  cd4099_latch cd4099_latch_3 (.R(or_1_out), .D(cd4099_adrdec_1_d), .WD(cd4099_adrdec_1_wd), .ZS(nand_3_out), .Q(Q2));
  cd4099_latch cd4099_latch_4 (.R(or_1_out), .D(cd4099_adrdec_1_d), .WD(cd4099_adrdec_1_wd), .ZS(nand_4_out), .Q(Q3));
  cd4099_latch cd4099_latch_5 (.R(or_1_out), .D(cd4099_adrdec_1_d), .WD(cd4099_adrdec_1_wd), .ZS(nand_5_out), .Q(Q4));
  cd4099_latch cd4099_latch_6 (.R(or_1_out), .D(cd4099_adrdec_1_d), .WD(cd4099_adrdec_1_wd), .ZS(nand_6_out), .Q(Q5));
  cd4099_latch cd4099_latch_7 (.R(or_1_out), .D(cd4099_adrdec_1_d), .WD(cd4099_adrdec_1_wd), .ZS(nand_7_out), .Q(Q6));
  cd4099_latch cd4099_latch_8 (.R(or_1_out), .D(cd4099_adrdec_1_d), .WD(cd4099_adrdec_1_wd), .ZS(nand_8_out), .Q(Q7));

  // Notes on the sheet:
  //   Start-up reset pulse
  //   CD4099 CMOS 8-bit addressable latch
endmodule

module cd4099_latch (
  input  R,
  input  D,
  input  WD,
  input  ZS,
  output Q
);

  wire buffer_1_out, buffer_2_out, nand_1_out, nand_2_out, nor_1_out, not_1_out, transmission_1_p4,
       transmission_2_p4;

  nor nor_1 (nor_1_out, WD, ZS);
  not not_1 (not_1_out, nor_1_out);
  buf buffer_1 (buffer_1_out, nor_1_out);
  nand nand_1 (nand_1_out, R, not_1_out);
  buf buffer_2 (buffer_2_out, transmission_1_p4);
  // Transmission_Gate transmission_1: pin names not known; wires that end beside it: D, not_1_out, buffer_1_out, transmission_1_p4
  // Transmission_Gate transmission_2: pin names not known; wires that end beside it: transmission_1_p4, buffer_1_out, not_1_out, transmission_2_p4
  not not_2 (transmission_2_p4, nand_2_out);
  nand nand_2 (nand_2_out, nand_1_out, buffer_2_out);
  not not_3 (Q, nand_2_out);
endmodule

module cd4099_adrdec (
  input  A0,
  input  A1,
  input  A2,
  input  DATA,
  input  WRITE_DISABLE,
  input  RESET,
  output A0_2,
  output nA0,
  output A1_2,
  output nA1,
  output A2_2,
  output nA2,
  output D,
  output WD,
  output R
);

  wire not_4_out, not_5_out, not_6_out;

  not not_1 (nA0, A0);
  not not_2 (nA1, A1);
  not not_3 (nA2, A2);
  not not_4 (not_4_out, DATA);
  not not_5 (not_5_out, WRITE_DISABLE);
  not not_6 (not_6_out, RESET);
  not not_7 (A0_2, nA0);
  not not_8 (A1_2, nA1);
  not not_9 (A2_2, nA2);
  not not_10 (D, not_4_out);
  not not_11 (WD, not_5_out);
  not not_12 (R, not_6_out);
endmodule

module cd4099_sreset (
  output Q
);

  wire buffer_1_out, buffer_2_out, buffer_3_out, buffer_4_out, j_k_ff_1_q, not_1_out;

  buf buffer_1 (buffer_1_out, 1'b1);
  buf buffer_2 (buffer_2_out, buffer_1_out);
  buf buffer_3 (buffer_3_out, buffer_2_out);
  buf buffer_4 (buffer_4_out, buffer_3_out);
  J_K_Flip_Flop j_k_ff_1 (.J(1'b1), .K(1'b0), .Q(j_k_ff_1_q), .preset(buffer_4_out));  // open: clk, Qn, en, reset
  not not_1 (not_1_out, j_k_ff_1_q);
  and and_1 (Q, not_1_out, buffer_4_out);

  // Notes on the sheet:
  //   Start-up reset
endmodule
