// Logisim project cd4511 test.circ as structural Verilog: 1 circuit, main circuit main
module main (
  input  in_1,
  input  in_2,
  input  in_3,
  input  in_4,
  input  in_5,
  input  in_6,
  input  in_7
);

  wire cd4511_1_qa, cd4511_1_qb, cd4511_1_qc, cd4511_1_qd, cd4511_1_qe, cd4511_1_qf, cd4511_1_qg;

  cd4511 cd4511_1 (
    .d1(in_1), .d2(in_2), .d3(in_3), .d4(in_4), .LT_prime(in_5), .BI_prime(in_6), .LE_prime(in_7),
    .Qa(cd4511_1_qa), .Qb(cd4511_1_qb), .Qc(cd4511_1_qc), .Qd(cd4511_1_qd), .Qe(cd4511_1_qe),
    .Qf(cd4511_1_qf), .Qg(cd4511_1_qg));
  _7_Segment_Display u_7_segment_display_1 (
    .g(cd4511_1_qg), .f(cd4511_1_qf), .a(cd4511_1_qa), .b(cd4511_1_qb), .e(cd4511_1_qe), .d(cd4511_1_qd),
    .c(cd4511_1_qc));  // open: dp
endmodule
