// Logisim project cd4511.circ as structural Verilog: 1 circuit, main circuit cd4511
module cd4511 (
  input  d1,
  input  d2,
  input  d3,
  input  d4,
  input  LT_prime,
  input  BI_prime,
  input  LE_prime,
  output Qa,
  output Qb,
  output Qc,
  output Qd,
  output Qe,
  output Qf,
  output Qg
);

  wire and_1_out, buffer_1_out, buffer_2_out, buffer_3_out, buffer_4_out, buffer_5_out, latch1_2_q,
       latch1_2_qn, latch1_3_q, latch1_3_qn, latch1_4_qn, latch1_q, latch1_qn, nand_1_out, nand_2_out,
       nand_3_out, nand_4_out, nand_5_out, nand_6_out, nand_7_out, nand_8_out, nand_9_out, nand_10_out,
       nand_11_out, nand_12_out, nand_13_out, nand_14_out, nand_15_out, nand_16_out, nand_17_out,
       nand_18_out, nand_19_out, nand_20_out, nand_21_out, nand_22_out, nand_23_out, nor_1_out, nor_2_out,
       not_1_out, not_2_out;

  buf buffer_1 (buffer_1_out, d1);
  buf buffer_2 (buffer_2_out, d2);
  buf buffer_3 (buffer_3_out, d3);
  buf buffer_4 (buffer_4_out, d4);
  buf buffer_5 (buffer_5_out, LT_prime);
  not not_1 (not_1_out, BI_prime);
  not not_2 (not_2_out, LE_prime);
  D_Flip_Flop latch1 (.clk(not_2_out), .D(buffer_1_out), .Q(latch1_q), .Qn(latch1_qn));  // open: preset, en, reset
  D_Flip_Flop latch1_2 (
    .clk(not_2_out), .D(buffer_2_out), .Q(latch1_2_q), .Qn(latch1_2_qn));  // open: preset, en, reset
  D_Flip_Flop latch1_3 (
    .clk(not_2_out), .D(buffer_3_out), .Q(latch1_3_q), .Qn(latch1_3_qn));  // open: preset, en, reset
  D_Flip_Flop latch1_4 (.clk(not_2_out), .D(buffer_4_out), .Qn(latch1_4_qn));  // open: Q, preset, en, reset
  nand nand_1 (nand_1_out, latch1_3_q, latch1_2_q, latch1_qn);
  nand nand_2 (nand_2_out, latch1_3_q, latch1_q, latch1_2_qn);
  nand nand_3 (nand_3_out, latch1_3_q, latch1_2_qn, latch1_qn);
  nand nand_4 (nand_4_out, latch1_3_qn, latch1_2_q, latch1_qn);
  nand nand_5 (nand_5_out, latch1_q, latch1_2_qn, latch1_3_qn);
  nor nor_1 (nor_1_out, not_1_out, nor_2_out);
  nor nor_2 (nor_2_out, latch1_4_qn, and_1_out);
  and and_1 (and_1_out, latch1_3_qn, latch1_2_qn);
  nand nand_6 (nand_6_out, latch1_q, latch1_4_qn, latch1_3_qn, latch1_2_qn);
  nand nand_7 (nand_7_out, latch1_2_q, latch1_3_qn);
  nand nand_8 (nand_8_out, latch1_q, latch1_2_q, latch1_3_q);
  nand nand_9 (nand_9_out, latch1_qn, latch1_2_qn, latch1_3_qn, latch1_4_qn);
  nand nand_10 (nand_10_out, nand_3_out, nand_1_out, nor_1_out, nand_6_out);
  nand nand_11 (nand_11_out, nand_1_out, nand_2_out, nor_1_out);
  nand nand_12 (nand_12_out, nand_4_out, nor_1_out);
  nand nand_13 (nand_13_out, nand_5_out, nand_3_out, nand_8_out, nor_1_out);
  nand nand_14 (nand_14_out, nor_1_out, nand_3_out, latch1_qn);
  nand nand_15 (nand_15_out, nand_6_out, nor_1_out, nand_8_out, nand_7_out);
  nand nand_16 (nand_16_out, nand_6_out, nor_1_out, nand_8_out, nand_9_out);
  buf buffer_6 (Qa, nand_17_out);
  nand nand_17 (nand_17_out, nand_10_out, buffer_5_out);
  nand nand_18 (nand_18_out, nand_11_out, buffer_5_out);
  buf buffer_7 (Qb, nand_18_out);
  nand nand_19 (nand_19_out, nand_12_out, buffer_5_out);
  buf buffer_8 (Qc, nand_19_out);
  buf buffer_9 (Qd, nand_20_out);
  nand nand_20 (nand_20_out, nand_13_out, buffer_5_out);
  buf buffer_10 (Qe, nand_21_out);
  nand nand_21 (nand_21_out, nand_14_out, buffer_5_out);
  nand nand_22 (nand_22_out, nand_15_out, buffer_5_out);
  buf buffer_11 (Qf, nand_22_out);
  buf buffer_12 (Qg, nand_23_out);
  nand nand_23 (nand_23_out, nand_16_out, buffer_5_out);

  // Notes on the sheet:
  //   CD4511
  //   BCD to 7-segment latch/decoder/driver
endmodule
