// Logisim project cd4532 test.circ as structural Verilog: 1 circuit, main circuit main
module main (
  input  in_1,
  input  in_2,
  input  in_3,
  input  in_4,
  input  in_5,
  input  in_6,
  input  in_7,
  input  in_8,
  input  enable
);

  wire cd4532_1_e_o, cd4532_1_gs, cd4532_1_q0, cd4532_1_q1, cd4532_1_q2;

  cd4532 cd4532_1 (
    .d0(in_1), .d1(in_2), .d2(in_3), .d3(in_4), .d4(in_5), .d5(in_6), .d6(in_7), .d7(in_8), .e_i(enable),
    .q0(cd4532_1_q0), .q1(cd4532_1_q1), .q2(cd4532_1_q2), .gs(cd4532_1_gs), .e_o(cd4532_1_e_o));
  LED led_1 (.in(cd4532_1_q0));
  LED led_2 (.in(cd4532_1_q1));
  LED led_3 (.in(cd4532_1_q2));
  LED led_4 (.in(cd4532_1_gs));
  LED led_5 (.in(cd4532_1_e_o));

  // Notes on the sheet:
  //   highest priority
  //   lowest priority
  //   data outputs
endmodule
