// Logisim project cd4532.circ as structural Verilog: 1 circuit, main circuit cd4532
module cd4532 (
  input  d0,
  input  d1,
  input  d2,
  input  d3,
  input  d4,
  input  d5,
  input  d6,
  input  d7,
  input  e_i,
  output q0,
  output q1,
  output q2,
  output gs,
  output e_o
);

  wire nand_1_out, nand_2_out, nand_3_out, nand_4_out, nand_5_out, nand_6_out, nand_7_out, nor_1_out,
       nor_2_out, not_1_out, not_2_out, not_3_out, not_4_out, not_5_out, not_6_out, not_7_out, not_8_out,
       not_9_out, not_10_out, not_11_out, not_12_out, not_13_out, or_1_out, or_2_out, or_3_out, or_4_out,
       or_5_out, or_6_out, or_7_out;

  not not_1 (not_1_out, d1);
  not not_2 (not_2_out, d2);
  not not_3 (not_3_out, d3);
  not not_4 (not_4_out, d4);
  not not_5 (not_5_out, d5);
  not not_6 (not_6_out, d6);
  not not_7 (not_7_out, d7);
  not not_8 (not_8_out, e_i);
  not not_9 (not_9_out, not_2_out);
  not not_10 (not_10_out, not_4_out);
  not not_11 (not_11_out, not_5_out);
  not not_12 (not_12_out, not_6_out);
  not not_13 (not_13_out, not_8_out);
  or or_1 (or_1_out, not_1_out, not_9_out, not_10_out, not_12_out);
  or or_2 (or_2_out, not_12_out, not_10_out, not_3_out);
  or or_3 (or_3_out, not_12_out, not_5_out);
  or or_4 (or_4_out, not_2_out, not_10_out, not_11_out);
  or or_5 (or_5_out, not_3_out, not_10_out, not_11_out);
  nor nor_1 (nor_1_out, d7, d6, d5, d4);
  nor nor_2 (nor_2_out, d3, d2, d1, d0);
  nand nand_1 (nand_1_out, or_1_out, or_2_out, or_3_out, not_7_out);
  nand nand_2 (nand_2_out, or_4_out, or_5_out, not_6_out, not_7_out);
  nand nand_3 (nand_3_out, not_4_out, not_5_out, not_6_out, not_7_out);
  or or_6 (or_6_out, ~nor_1_out, ~nor_2_out);  // OR_Gate
  or or_7 (or_7_out, ~nor_2_out, ~nor_1_out, ~e_i);  // OR_Gate
  nand nand_4 (nand_4_out, or_6_out, e_i);
  nand nand_5 (nand_5_out, nand_1_out, not_13_out);
  not not_14 (q0, nand_5_out);
  not not_15 (q1, nand_6_out);
  nand nand_6 (nand_6_out, nand_2_out, not_13_out);
  nand nand_7 (nand_7_out, nand_3_out, not_13_out);
  not not_16 (q2, nand_7_out);
  not not_17 (gs, nand_4_out);
  not not_18 (e_o, or_7_out);

  // Notes on the sheet:
  //   CD4532: 8-bit priority encoder
endmodule
