// Logisim project cd4555 test.circ as structural Verilog: 1 circuit, main circuit main
module main (
  input  in_1,
  input  in_2,
  input  in_3,
  input  in_4,
  input  in_5,
  input  in_6
);

  wire cd4555_1__1q0, cd4555_1__1q1, cd4555_1__1q2, cd4555_1__1q3, cd4555_1__2q0, cd4555_1__2q1,
       cd4555_1__2q2, cd4555_1__2q3;

  cd4555 cd4555_1 (
    ._1A(in_1), ._1B(in_2), .n1E(in_3), ._2A(in_4), ._2B(in_5), .n2E(in_6), ._1Q0(cd4555_1__1q0),
    ._1Q1(cd4555_1__1q1), ._1Q2(cd4555_1__1q2), ._1Q3(cd4555_1__1q3), ._2Q0(cd4555_1__2q0),
    ._2Q1(cd4555_1__2q1), ._2Q2(cd4555_1__2q2), ._2Q3(cd4555_1__2q3));
  LED led_1 (.in(cd4555_1__1q0));
  LED led_2 (.in(cd4555_1__1q1));
  LED led_3 (.in(cd4555_1__1q2));
  LED led_4 (.in(cd4555_1__1q3));
  LED led_5 (.in(cd4555_1__2q0));
  LED led_6 (.in(cd4555_1__2q1));
  LED led_7 (.in(cd4555_1__2q2));
  LED led_8 (.in(cd4555_1__2q3));
endmodule
