// Logisim project cd4555.circ as structural Verilog: 2 circuits, main circuit cd4555_demux
module cd4555_demux (
  input  A,
  input  B,
  input  nE,
  output Q0,
  output Q1,
  output Q2,
  output Q3
);

  wire not_1_out, not_2_out, not_3_out, not_4_out, not_5_out;

  not not_1 (not_1_out, A);
  not not_2 (not_2_out, B);
  not not_3 (not_3_out, nE);
  not not_4 (not_4_out, not_1_out);
  not not_5 (not_5_out, not_2_out);
  and and_1 (Q0, not_1_out, not_2_out, not_3_out);
  and and_2 (Q1, not_4_out, not_2_out, not_3_out);
  and and_3 (Q2, not_1_out, not_5_out, not_3_out);
  and and_4 (Q3, not_4_out, not_5_out, not_3_out);

  // Notes on the sheet:
  //   Binary to 1-of-4 decoder/demultiplexer
endmodule

module cd4555 (
  input  _1A,
  input  _1B,
  input  n1E,
  input  _2A,
  input  _2B,
  input  n2E,
  output _1Q0,
  output _1Q1,
  output _1Q2,
  output _1Q3,
  output _2Q0,
  output _2Q1,
  output _2Q2,
  output _2Q3
);

  cd4555_demux cd4555_demux_1 (.A(_1A), .B(_1B), .nE(n1E), .Q0(_1Q0), .Q1(_1Q1), .Q2(_1Q2), .Q3(_1Q3));
  cd4555_demux cd4555_demux_2 (.A(_2A), .B(_2B), .nE(n2E), .Q0(_2Q0), .Q1(_2Q1), .Q2(_2Q2), .Q3(_2Q3));

  // Notes on the sheet:
  //   CD4555: Dual binary to 1-of-4 decoder/multiplexer
endmodule
