// Logisim project kaikkinollat.circ as structural Verilog: 1 circuit, main circuit a2
module a2 (
  input  A,
  input  B,
  input  C,
  output out_4
);

  wire nor_1_out, nor_2_out, not_1_out;

  nor nor_1 (nor_1_out, A, B);
  not not_1 (not_1_out, nor_1_out);
  nor nor_2 (nor_2_out, not_1_out, C);
  not not_2 (out_4, nor_2_out);
endmodule
