// Logisim project sarjavilkku.circ as structural Verilog: 1 circuit, main circuit main
module main (
  input  in_1
);

  wire clock_1_out, j_k_ff_1_q, n74f374_1_q0, n74f374_1_q1, n74f374_1_q2, n74f374_1_q3, n74f374_1_q4,
       n74f374_1_q5, n74f374_1_q6, n74f374_1_q7, nand_1_out, nand_2_out, nand_3_out, nand_4_out, not_1_out,
       not_2_out;

  Clock clock_1 (.out(clock_1_out));
  _74F374 u_74f374_1 (
    .nCP(clock_1_out), .nOE(in_1), .D0(j_k_ff_1_q), .D1(n74f374_1_q0), .D2(n74f374_1_q1), .D3(n74f374_1_q2),
    .D4(n74f374_1_q3), .D5(n74f374_1_q4), .D6(n74f374_1_q5), .D7(n74f374_1_q6), .Q0(n74f374_1_q0),
    .Q1(n74f374_1_q1), .Q2(n74f374_1_q2), .Q3(n74f374_1_q3), .Q4(n74f374_1_q4), .Q5(n74f374_1_q5),
    .Q6(n74f374_1_q6), .Q7(n74f374_1_q7));
  nand nand_1 (nand_1_out, n74f374_1_q7, n74f374_1_q0);
  nand nand_2 (nand_2_out, nand_1_out, nand_1_out);
  not not_1 (not_1_out, n74f374_1_q0);
  nand nand_3 (nand_3_out, not_1_out, not_2_out);
  not not_2 (not_2_out, n74f374_1_q7);
  J_K_Flip_Flop j_k_ff_1 (
    .J(nand_4_out), .clk(clock_1_out), .K(nand_2_out), .Q(j_k_ff_1_q));  // open: Qn, preset, en, reset
  nand nand_4 (nand_4_out, nand_3_out, nand_3_out);
  LED led_1 (.in(n74f374_1_q1));
  LED led_2 (.in(n74f374_1_q0));
  LED led_3 (.in(n74f374_1_q2));
  LED led_4 (.in(n74f374_1_q3));
  LED led_5 (.in(n74f374_1_q5));
  LED led_6 (.in(n74f374_1_q4));
  LED led_7 (.in(n74f374_1_q7));
  LED led_8 (.in(n74f374_1_q6));

  // Notes on the sheet:
  //   "Ending" condition
  //   Barrier serial flasher, 8 lamps
  //   Memory bit
  //   "Begin" condition
  //   Barrier lamps
endmodule
