// Logisim project shift register 74f374.circ as structural Verilog: 1 circuit, main circuit main
module main (
  input  nOUTPUT_ENABLE,
  input  latch_cp,
  input  nlatch_oe,
  input  CLOCK_IN,
  input  DATA_IN
);

  wire n74f374_1_q0, n74f374_1_q1, n74f374_1_q2, n74f374_1_q3, n74f374_1_q4, n74f374_1_q5, n74f374_1_q6,
       n74f374_1_q7, n74f374_2_q0, n74f374_2_q1, n74f374_2_q2, n74f374_2_q3, n74f374_2_q4, n74f374_2_q5,
       n74f374_2_q6, n74f374_2_q7;

  _74F374 u_74f374_1 (
    .nCP(CLOCK_IN), .nOE(1'b0), .D0(DATA_IN), .D1(n74f374_1_q0), .D2(n74f374_1_q1), .D3(n74f374_1_q2),
    .D4(n74f374_1_q3), .D5(n74f374_1_q4), .D6(n74f374_1_q5), .D7(n74f374_1_q6), .Q0(n74f374_1_q0),
    .Q1(n74f374_1_q1), .Q2(n74f374_1_q2), .Q3(n74f374_1_q3), .Q4(n74f374_1_q4), .Q5(n74f374_1_q5),
    .Q6(n74f374_1_q6), .Q7(n74f374_1_q7));
  _74F374 u_74f374_2 (
    .nCP(latch_cp), .nOE(nlatch_oe), .D0(n74f374_1_q0), .D1(n74f374_1_q1), .D2(n74f374_1_q2),
    .D3(n74f374_1_q3), .D4(n74f374_1_q4), .D5(n74f374_1_q5), .D6(n74f374_1_q6), .D7(n74f374_1_q7),
    .Q0(n74f374_2_q0), .Q1(n74f374_2_q1), .Q2(n74f374_2_q2), .Q3(n74f374_2_q3), .Q4(n74f374_2_q4),
    .Q5(n74f374_2_q5), .Q6(n74f374_2_q6), .Q7(n74f374_2_q7));
  LED led_1 (.in(n74f374_1_q0));
  LED led_2 (.in(n74f374_1_q1));
  LED led_3 (.in(n74f374_1_q2));
  LED led_4 (.in(n74f374_1_q3));
  LED led_5 (.in(n74f374_1_q4));
  LED led_6 (.in(n74f374_1_q5));
  LED led_7 (.in(n74f374_1_q6));
  LED led_8 (.in(n74f374_1_q7));
  LED led_9 (.in(n74f374_2_q0));
  LED led_10 (.in(n74f374_2_q1));
  LED led_11 (.in(n74f374_2_q2));
  LED led_12 (.in(n74f374_2_q3));
  LED led_13 (.in(n74f374_2_q4));
  LED led_14 (.in(n74f374_2_q5));
  LED led_15 (.in(n74f374_2_q6));
  LED led_16 (.in(n74f374_2_q7));

  // Notes on the sheet:
  //   8-bit shift register with output latch
  //   Shift register
  //   Output latch
endmodule
